# Fritzing sketch Board (saved by Fritzing 0.9.10b)
breadboards: 3

parts:
  U1 = ESP32S-HiLetgo [part_number=ESP32S-HiLetgo]
  HC-SR04_Sensor_1 = HC-SR04 Ultrasonic Distance Sensor
  LCD1 = LCD screen
  S1 = Pushbutton [package="[THT]"]
  R1 = Trimmer Potentiometer [maximum_resistance=10kΩ knob_status=50% power=0.5W package=THT]
  ZS-042_RTC1 = ZS-042 RTC Module
  SD_card_module1 = SD Card Module
  R2 = Resistor [tolerance=±5% power=0.25 resistance=10k package=THT]

nets:
  VCC: U1.3.3, HC-SR04_Sensor_1.VCC, S1.Pin_1, S1.Pin_2, ZS-042_RTC1.VCC, SD_card_module1.+3.3
  N1: U1.GPIO35, S1.Pin_3, S1.Pin_4, R2.Pin_1
  N2: U1.GPIO32, LCD1.RS
  N3: U1.GPIO33, LCD1.E
  N4: U1.GPIO25, LCD1.DB4
  N5: U1.GPIO26, LCD1.DB5
  N6: U1.GPIO27, LCD1.DB6
  N7: U1.GPIO14, LCD1.DB7
  N8: U1.GPIO12, LCD1.LED+
  GND: U1.GND, HC-SR04_Sensor_1.GND, LCD1.VSS, LCD1.R/W, LCD1.LED-, R1.leg2, ZS-042_RTC1.GND, SD_card_module1.GND#0, R2.Pin_0
  N9: U1.VIN, R1.leg1
  N10: U1.GPIO16, HC-SR04_Sensor_1.ECHO
  N11: U1.GPIO17, HC-SR04_Sensor_1.TRIG
  N12: U1.GPIO5, SD_card_module1.CS
  N13: U1.GPIO18, SD_card_module1.SCK
  N14: U1.GPIO19, SD_card_module1.MISO
  N15: U1.GPIO21, ZS-042_RTC1.SDA
  N16: U1.GPIO22, ZS-042_RTC1.SCL
  N17: U1.GPIO23, SD_card_module1.MOSI
  N18: LCD1.V0, R1.wiper

custom parts:
  ESP32S-HiLetgo: HiLetgo ESP-WROOM-32 ESP32 ESP-32S Development Board 2.4GHz Dual-Mode WiFi + Bluetooth Dual Cores Microcontroller The ESP32 integrated with Antenna switches, RF Balun, power amplifiers, low-noise amplifiers, filters, and management modules, and the entire solution occupies the least area of PCB. 2.4 GHz Wi-Fi plus Bluetooth dual-mode chip, with TSMC Ultra-low power consumption 40nm technology,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
  SD Card Module: SD Card Module Slot Socket Reader For Arduino ARM MCU

// code stored in the sketch: Untitled.ino

